// Logisim project ULA.circ as structural Verilog
module meiosomador (
  input  in_1,
  input  in_2,
  output out_3,
  output out_4
);

  xor Soma (out_3, in_1, in_2);
  and Carry_In (out_4, in_1, in_2);
endmodule

module somadorcompleto (
  input  Cin,
  input  A,
  input  B,
  output \Saída_Soma ,
  output Cout
);

  wire A___B_out, A___Cin_out, B__Cin_out, Soma_out;

  xor Soma (Soma_out, A, B);
  and A___B (A___B_out, A, B);
  and A___Cin (A___Cin_out, A, Cin);
  and B__Cin (B__Cin_out, B, Cin);
  xor plus_Cin (\Saída_Soma , Cin, Soma_out);
  or Out (Cout, A___B_out, A___Cin_out, B__Cin_out);
endmodule

module MUX32 (
  input  E0,
  input  E1,
  input  E2,
  input  E3,
  input  E4,
  input  E5,
  input  E6,
  input  E7,
  input  E8,
  input  E9,
  input  E10,
  input  E11,
  input  E12,
  input  E13,
  input  E14,
  input  E15,
  input  E16,
  input  E17,
  input  E18,
  input  E19,
  input  E20,
  input  E21,
  input  E22,
  input  E23,
  input  E24,
  input  E25,
  input  E26,
  input  E27,
  input  E28,
  input  E29,
  input  E30,
  input  E31,
  input  B,
  input  A,
  input  D,
  input  C,
  input  E,
  output out_38
);

  wire mux16_1_out_21, mux16_2_out_21;

  MUX16 mux16_1 (
    .E0(E0), .E1(E1), .E2(E2), .E3(E3), .E4(E4), .E5(E5), .E6(E6), .E7(E7), .E8(E8), .E9(E9), .E10(E10),
    .E11(E11), .E12(E12), .E13(E13), .E14(E14), .E15(E15), .C(B), .D(A), .A(D), .B(C), .out_21(mux16_1_out_21));
  MUX16 mux16_2 (
    .E0(E16), .E1(E17), .E2(E18), .E3(E19), .E4(E20), .E5(E21), .E6(E22), .E7(E23), .E8(E24), .E9(E25),
    .E10(E26), .E11(E27), .E12(E28), .E13(E29), .E14(E30), .E15(E31), .C(B), .D(A), .A(D), .B(C),
    .out_21(mux16_2_out_21));
  MUX2 mux2_1 (.E0(mux16_1_out_21), .E1(mux16_2_out_21), .E(E), .out_4(out_38));
endmodule

module MUX4 (
  input  in_1,
  input  in_2,
  input  in_3,
  input  in_4,
  input  in_5,
  input  in_6,
  output out_7
);

  wire and_1_out, and_2_out, and_3_out, and_4_out;

  and and_1 (and_1_out, in_1, ~in_5, ~in_6);  // AND_Gate
  and and_2 (and_2_out, in_2, ~in_5, in_6);  // AND_Gate
  and and_3 (and_3_out, in_3, in_5, ~in_6);  // AND_Gate
  and and_4 (and_4_out, in_4, in_5, in_6);
  or or_1 (out_7, and_1_out, and_2_out, and_3_out, and_4_out);
endmodule

module MUX16 (
  input  E0,
  input  E1,
  input  E2,
  input  E3,
  input  E4,
  input  E5,
  input  E6,
  input  E7,
  input  E8,
  input  E9,
  input  E10,
  input  E11,
  input  E12,
  input  E13,
  input  E14,
  input  E15,
  input  C,
  input  D,
  input  A,
  input  B,
  output out_21
);

  wire mux4_1_out_7, mux4_2_out_7, mux4_3_out_7, mux4_4_out_7;

  MUX4 mux4_1 (.in_1(E0), .in_2(E1), .in_3(E2), .in_4(E3), .in_5(C), .in_6(D), .out_7(mux4_1_out_7));
  MUX4 mux4_2 (.in_1(E4), .in_2(E5), .in_3(E6), .in_4(E7), .in_5(C), .in_6(D), .out_7(mux4_2_out_7));
  MUX4 mux4_3 (.in_1(E8), .in_2(E9), .in_3(E10), .in_4(E11), .in_5(C), .in_6(D), .out_7(mux4_3_out_7));
  MUX4 mux4_4 (.in_1(E12), .in_2(E13), .in_3(E14), .in_4(E15), .in_5(C), .in_6(D), .out_7(mux4_4_out_7));
  MUX4 mux4_5 (
    .in_1(mux4_1_out_7), .in_2(mux4_2_out_7), .in_3(mux4_3_out_7), .in_4(mux4_4_out_7), .in_5(A), .in_6(B),
    .out_7(out_21));
endmodule

module MUX2 (
  input  E0,
  input  E1,
  input  E,
  output out_4
);

  wire and_1_out, and_2_out;

  and and_1 (and_1_out, E0, ~E);  // AND_Gate
  and and_2 (and_2_out, E1, E);
  or or_1 (out_4, and_1_out, and_2_out);
endmodule

module \CélulaULA  (
  input  A,
  input  B,
  input  Cin,
  input  [2:0] in_4,
  output out_5,
  output Cout
);

  wire and_1_out, or_1_out, \somadorcompleto_1_saída_soma , xor_1_out;

  and and_1 (and_1_out, A, B);
  or or_1 (or_1_out, A, B);
  xor xor_1 (xor_1_out, A, B);
  somadorcompleto somadorcompleto_1 (
    .Cin(Cin), .A(A), .B(B), .\Saída_Soma (\somadorcompleto_1_saída_soma ), .Cout(Cout));
  MUX8 mux8_1 (
    .E0(and_1_out), .E1(or_1_out), .E2(\somadorcompleto_1_saída_soma ), .E3(xor_1_out), .E4(A), .E5(A),
    .E6(A), .B(in_4[2]), .C(in_4[1]), .A(in_4[0]), .out_12(out_5));  // open: E7
endmodule

module somador_32_bits (
  input  A0,
  input  B0,
  input  A0_2,
  input  B0_2,
  input  A0_3,
  input  B0_3,
  input  A0_4,
  input  B0_4,
  input  A0_5,
  input  B0_5,
  input  A0_6,
  input  B0_6,
  input  A0_7,
  input  B0_7,
  input  A0_8,
  input  B0_8,
  input  A0_9,
  input  B0_9,
  input  A0_10,
  input  B0_10,
  input  A0_11,
  input  B0_11,
  input  A0_12,
  input  B0_12,
  input  A0_13,
  input  B0_13,
  input  A2,
  input  B2,
  input  A1,
  input  B1,
  input  A0_14,
  input  B0_14,
  input  A0_15,
  input  B0_15,
  input  A0_16,
  input  B0_16,
  input  A0_17,
  input  B0_17,
  input  A0_18,
  input  B0_18,
  input  A0_19,
  input  B0_19,
  input  A0_20,
  input  B0_20,
  input  A0_21,
  input  B0_21,
  input  A0_22,
  input  B0_22,
  input  A0_23,
  input  B0_23,
  input  A0_24,
  input  B0_24,
  input  A0_25,
  input  B0_25,
  input  A0_26,
  input  B0_26,
  input  A0_27,
  input  B0_27,
  input  A0_28,
  input  B0_28,
  input  A0_29,
  input  B0_29,
  input  A0_30,
  input  B0_30,
  input  Cin0,
  output Cout31,
  output Soma31,
  output Soma30,
  output Soma29,
  output Soma28,
  output Soma27,
  output Soma26,
  output Soma25,
  output Soma24,
  output Soma23,
  output Soma22,
  output Soma21,
  output Soma20,
  output Soma19,
  output Soma18,
  output Soma17,
  output Soma16,
  output Soma15,
  output Soma14,
  output Soma13,
  output Soma12,
  output Soma11,
  output Soma10,
  output Soma9,
  output Soma8,
  output Soma7,
  output Soma6,
  output Soma5,
  output Soma4,
  output Soma3,
  output Soma2,
  output Soma1,
  output Soma0
);

  wire somadorcompleto_2_cout, somadorcompleto_3_cout, somadorcompleto_4_cout, somadorcompleto_5_cout,
       somadorcompleto_6_cout, somadorcompleto_7_cout, somadorcompleto_8_cout, somadorcompleto_9_cout,
       somadorcompleto_10_cout, somadorcompleto_11_cout, somadorcompleto_12_cout, somadorcompleto_13_cout,
       somadorcompleto_14_cout, somadorcompleto_15_cout, somadorcompleto_16_cout, somadorcompleto_17_cout,
       somadorcompleto_18_cout, somadorcompleto_19_cout, somadorcompleto_20_cout, somadorcompleto_21_cout,
       somadorcompleto_22_cout, somadorcompleto_23_cout, somadorcompleto_24_cout, somadorcompleto_25_cout,
       somadorcompleto_26_cout, somadorcompleto_27_cout, somadorcompleto_28_cout, somadorcompleto_29_cout,
       somadorcompleto_30_cout, somadorcompleto_31_cout, somadorcompleto_32_cout;

  somadorcompleto somadorcompleto_1 (
    .Cin(somadorcompleto_2_cout), .A(A0_15), .B(B0_15), .\Saída_Soma (Soma31), .Cout(Cout31));
  somadorcompleto somadorcompleto_2 (
    .Cin(somadorcompleto_3_cout), .A(A0_16), .B(B0_16), .\Saída_Soma (Soma30), .Cout(somadorcompleto_2_cout));
  somadorcompleto somadorcompleto_3 (
    .Cin(somadorcompleto_4_cout), .A(A0_17), .B(B0_17), .\Saída_Soma (Soma29), .Cout(somadorcompleto_3_cout));
  somadorcompleto somadorcompleto_4 (
    .Cin(somadorcompleto_5_cout), .A(A0_18), .B(B0_18), .\Saída_Soma (Soma28), .Cout(somadorcompleto_4_cout));
  somadorcompleto somadorcompleto_5 (
    .Cin(somadorcompleto_6_cout), .A(A0_19), .B(B0_19), .\Saída_Soma (Soma27), .Cout(somadorcompleto_5_cout));
  somadorcompleto somadorcompleto_6 (
    .Cin(somadorcompleto_7_cout), .A(A0_20), .B(B0_20), .\Saída_Soma (Soma26), .Cout(somadorcompleto_6_cout));
  somadorcompleto somadorcompleto_7 (
    .Cin(somadorcompleto_8_cout), .A(A0_21), .B(B0_21), .\Saída_Soma (Soma25), .Cout(somadorcompleto_7_cout));
  somadorcompleto somadorcompleto_8 (
    .Cin(somadorcompleto_9_cout), .A(A0_22), .B(B0_22), .\Saída_Soma (Soma24), .Cout(somadorcompleto_8_cout));
  somadorcompleto somadorcompleto_9 (
    .Cin(somadorcompleto_10_cout), .A(A0_23), .B(B0_23), .\Saída_Soma (Soma23), .Cout(somadorcompleto_9_cout));
  somadorcompleto somadorcompleto_10 (
    .Cin(somadorcompleto_11_cout), .A(A0_24), .B(B0_24), .\Saída_Soma (Soma22), .Cout(somadorcompleto_10_cout));
  somadorcompleto somadorcompleto_11 (
    .Cin(somadorcompleto_12_cout), .A(A0_25), .B(B0_25), .\Saída_Soma (Soma21), .Cout(somadorcompleto_11_cout));
  somadorcompleto somadorcompleto_12 (
    .Cin(somadorcompleto_13_cout), .A(A0_26), .B(B0_26), .\Saída_Soma (Soma20), .Cout(somadorcompleto_12_cout));
  somadorcompleto somadorcompleto_13 (
    .Cin(somadorcompleto_14_cout), .A(A0_27), .B(B0_27), .\Saída_Soma (Soma19), .Cout(somadorcompleto_13_cout));
  somadorcompleto somadorcompleto_14 (
    .Cin(somadorcompleto_15_cout), .A(A0_28), .B(B0_28), .\Saída_Soma (Soma18), .Cout(somadorcompleto_14_cout));
  somadorcompleto somadorcompleto_15 (
    .Cin(somadorcompleto_16_cout), .A(A0_29), .B(B0_29), .\Saída_Soma (Soma17), .Cout(somadorcompleto_15_cout));
  somadorcompleto somadorcompleto_16 (
    .Cin(somadorcompleto_17_cout), .A(A0_30), .B(B0_30), .\Saída_Soma (Soma16), .Cout(somadorcompleto_16_cout));
  somadorcompleto somadorcompleto_17 (
    .Cin(somadorcompleto_18_cout), .A(A0), .B(B0), .\Saída_Soma (Soma15), .Cout(somadorcompleto_17_cout));
  somadorcompleto somadorcompleto_18 (
    .Cin(somadorcompleto_19_cout), .A(A0_2), .B(B0_2), .\Saída_Soma (Soma14), .Cout(somadorcompleto_18_cout));
  somadorcompleto somadorcompleto_19 (
    .Cin(somadorcompleto_20_cout), .A(A0_3), .B(B0_3), .\Saída_Soma (Soma13), .Cout(somadorcompleto_19_cout));
  somadorcompleto somadorcompleto_20 (
    .Cin(somadorcompleto_21_cout), .A(A0_4), .B(B0_4), .\Saída_Soma (Soma12), .Cout(somadorcompleto_20_cout));
  somadorcompleto somadorcompleto_21 (
    .Cin(somadorcompleto_22_cout), .A(A0_5), .B(B0_5), .\Saída_Soma (Soma11), .Cout(somadorcompleto_21_cout));
  somadorcompleto somadorcompleto_22 (
    .Cin(somadorcompleto_23_cout), .A(A0_6), .B(B0_6), .\Saída_Soma (Soma10), .Cout(somadorcompleto_22_cout));
  somadorcompleto somadorcompleto_23 (
    .Cin(somadorcompleto_24_cout), .A(A0_7), .B(B0_7), .\Saída_Soma (Soma9), .Cout(somadorcompleto_23_cout));
  somadorcompleto somadorcompleto_24 (
    .Cin(somadorcompleto_25_cout), .A(A0_8), .B(B0_8), .\Saída_Soma (Soma8), .Cout(somadorcompleto_24_cout));
  somadorcompleto somadorcompleto_25 (
    .Cin(somadorcompleto_26_cout), .A(A0_9), .B(B0_9), .\Saída_Soma (Soma7), .Cout(somadorcompleto_25_cout));
  somadorcompleto somadorcompleto_26 (
    .Cin(somadorcompleto_27_cout), .A(A0_10), .B(B0_10), .\Saída_Soma (Soma6), .Cout(somadorcompleto_26_cout));
  somadorcompleto somadorcompleto_27 (
    .Cin(somadorcompleto_28_cout), .A(A0_11), .B(B0_11), .\Saída_Soma (Soma5), .Cout(somadorcompleto_27_cout));
  somadorcompleto somadorcompleto_28 (
    .Cin(somadorcompleto_29_cout), .A(A0_12), .B(B0_12), .\Saída_Soma (Soma4), .Cout(somadorcompleto_28_cout));
  somadorcompleto somadorcompleto_29 (
    .Cin(somadorcompleto_30_cout), .A(A0_13), .B(B0_13), .\Saída_Soma (Soma3), .Cout(somadorcompleto_29_cout));
  somadorcompleto somadorcompleto_30 (
    .Cin(somadorcompleto_31_cout), .A(A2), .B(B2), .\Saída_Soma (Soma2), .Cout(somadorcompleto_30_cout));
  somadorcompleto somadorcompleto_31 (
    .Cin(somadorcompleto_32_cout), .A(A1), .B(B1), .\Saída_Soma (Soma1), .Cout(somadorcompleto_31_cout));
  somadorcompleto somadorcompleto_32 (
    .Cin(Cin0), .A(A0_14), .B(B0_14), .\Saída_Soma (Soma0), .Cout(somadorcompleto_32_cout));
endmodule

module MUX8 (
  input  E0,
  input  E1,
  input  E2,
  input  E3,
  input  E4,
  input  E5,
  input  E6,
  input  E7,
  input  B,
  input  C,
  input  A,
  output out_12
);

  wire mux4_1_out_7, mux4_2_out_7;

  MUX4 mux4_1 (.in_1(E0), .in_2(E1), .in_3(E2), .in_4(E3), .in_5(B), .in_6(C), .out_7(mux4_1_out_7));
  MUX4 mux4_2 (.in_1(E4), .in_2(E5), .in_3(E6), .in_4(E7), .in_5(B), .in_6(C), .out_7(mux4_2_out_7));
  MUX2 mux2_1 (.E0(mux4_1_out_7), .E1(mux4_2_out_7), .E(A), .out_4(out_12));
endmodule
